# Fritzing sketch 4bitCounter (saved by Fritzing 0.9.3b)
breadboards: 1

parts:
  Parça1 = Arduino Uno (Rev3)
  R1 = Resistor [tolerance=±5% resistance=220 package=THT]
  R2 = Resistor [tolerance=±5% resistance=220 package=THT]
  R3 = Resistor [tolerance=±5% resistance=220 package=THT]
  R4 = Resistor [tolerance=±5% resistance=220 package=THT]
  LED1 = LED - 5mm [color="Red (633nm)" package="5 mm [THT]"]
  LED2 = LED - 5mm [color="Red (633nm)" package="5 mm [THT]"]
  LED3 = LED - 5mm [color="Red (633nm)" package="5 mm [THT]"]
  LED4 = LED - 5mm [color="Red (633nm)" package="5 mm [THT]"]

nets:
  N1: Parça1.D9_PWM, LED4.anode
  N2: Parça1.D10_PWM/SS, LED3.anode
  N3: Parça1.D11_PWM/MOSI, LED2.anode
  N4: Parça1.D12/MISO, LED1.anode
  N5: Parça1.GND, R1.Pin_1, R2.Pin_1, R3.Pin_1, R4.Pin_1
  N6: R1.Pin_0, LED1.cathode
  N7: R2.Pin_0, LED2.cathode
  N8: R3.Pin_0, LED4.cathode
  N9: R4.Pin_0, LED3.cathode
