# Fritzing sketch Blink_Speed_Without_Map_Code (saved by Fritzing 0.9.3b)
breadboards: 1

parts:
  Parça1 = Arduino Uno (Rev3)
  R1 = Resistor [tolerance=±5% resistance=220 package=THT]
  LED1 = LED - 5mm [color="Red (633nm)" package="5 mm [THT]"]
  R2 = Rotary Potentiometer (Small) [maximum_resistance=100kΩ package=THT]

nets:
  N1: Parça1.A0, R2.wiper
  N2: Parça1.D9_PWM, LED1.anode
  N3: Parça1.5V, R2.leg1
  N4: Parça1.GND, R1.Pin_0, R2.leg2
  N5: R1.Pin_1, LED1.cathode
