# Fritzing sketch 7 segment (saved by Fritzing 0.9.3b)
breadboards: 1

parts:
  U1 = 7-SEGMENT-DISPLAY [package=7-segment-display]
  Parça1 = Arduino Uno (Rev3)
  R1 = Resistor [tolerance=±5% resistance=220 package=THT]
  R2 = Resistor [tolerance=±5% resistance=220 package=THT]
  R3 = Resistor [tolerance=±5% resistance=220 package=THT]
  R4 = Resistor [tolerance=±5% resistance=220 package=THT]
  R5 = Resistor [tolerance=±5% resistance=220 package=THT]
  R6 = Resistor [tolerance=±5% resistance=220 package=THT]
  R7 = Resistor [tolerance=±5% resistance=220 package=THT]

nets:
  N1: U1.E, R5.Pin_1
  N2: U1.D, R4.Pin_1
  N3: U1.C, R3.Pin_1
  N4: U1.B, R2.Pin_1
  N5: U1.A, R1.Pin_1
  N6: U1.F, R6.Pin_1
  N7: U1.G, R7.Pin_1
  N8: Parça1.D1/TX, R1.Pin_0
  N9: Parça1.D2, R2.Pin_0
  N10: Parça1.D3_PWM, R3.Pin_0
  N11: Parça1.D4, R4.Pin_0
  N12: Parça1.D5_PWM, R5.Pin_0
  N13: Parça1.D6_PWM, R6.Pin_0
  N14: Parça1.D7, R7.Pin_0
